# Fritzing sketch Push Button Start (saved by Fritzing 0.9.3b)
breadboards: 1

parts:
  LED1 = LED - 5mm [color="Red (633nm)" package="5 mm [THT]"]
  S1 = Pushbutton [package="[THT]"]
  U1 = 4-Channel 5v Relay Shield [package=relay-4ch5v10a]
  Part1 = Adafruit Metro Mini [part_number="Adafruit #2590"]
  R1 = Resistor [tolerance=±5% resistance=220 package=THT]
  V1 = DC Power [voltage=12V]
  S2 = Toggle Switch [package=THT]
  Q2 = Basic FET N-Channel [package="TO220 [THT]"]

nets:
  N1: LED1.cathode, Q2.drain
  N2: LED1.anode, Part1.VIN, V1.V+
  GND: S1.Pin_1, S1.Pin_2, U1.GND, Part1.GND, V1.V-, S2.COM, Q2.source
  N3: S1.Pin_3, S1.Pin_4, Part1.IO2
  VCC: U1.VCC, Part1.+5V
  N4: U1.IN1, Part1.IO5
  N5: U1.IN2, Part1.IO6
  N6: U1.IN4, Part1.IO8
  N7: U1.IN3, Part1.IO7
  N8: Part1.IO9, R1.Pin_0
  N9: Part1.IO3, S2.L1
  N10: R1.Pin_1, Q2.gate

notes:
  killswitch
  4ch Relay Board
  push start
  Vin - 12V

custom parts:
  4-Channel 5v Relay Shield: 4 Channel 5v Relay Shield w. 2x SPD-06VDC-SD-C
  Adafruit Metro Mini: We sure love the ATmega328 here at Adafruit, and we use them a lot for our own projects. The processor has plenty of GPIO, Analog inputs, hardware UART SPI and I2C, timers and PWM galore - just enough for most simple projects. When we need to go small, we use a Pro Trinket 3V or 5V, but if you want to have USB-to-Serial built in, we reach for an Adafruit METRO Mini. METRO Mini is the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
